# Fritzing sketch Circuit Diagram (saved by Fritzing 0.9.3b)
breadboards: 2

parts:
  L298N1 = L298N DC motor driver
  Part2 = Arduino Mega 2560 (Rev3)
  L298N2 = L298N DC motor driver
  M3 = DC Motor
  M4 = DC Motor
  M5 = DC Motor
  M6 = DC Motor
  M7 = DC Motor
  M8 = DC Motor
  D1 = Diode [package=diode-1n4148]
  D2 = Diode [package=diode-1n4148]
  D3 = Diode [package=diode-1n4148]
  D4 = Diode [package=diode-1n4148]
  D5 = Diode [package=diode-1n4148]
  D6 = Diode [package=diode-1n4148]
  123sda = MSGEQ7 [package=soic8]
  LED1 = smd LED [color="Red (633nm)" package="0805 [SMD]"]
  LED2 = smd LED [color="Yellow (595nm)" package="0805 [SMD]"]
  R1 = Resistor [tolerance=±5% resistance=220 package=THT]  # not connected
  R2 = Resistor [tolerance=±5% resistance=220 package=THT]
  Water_Level_Sensor1 = Water Level Sensor
  SP1 = SPEAKER [package=pcb_mount_speaker]  # not connected
  VCC2 = Battery
  VCC1 = 4 x AAA Battery Mount

nets:
  N1: L298N1.OUT1, M3.pin_1
  N2: L298N1.OUT2, M5.pin_1
  N3: L298N1.OUT3, M4.pin_1
  N4: L298N1.OUT4, M7.pin_1
  12V: L298N1.12V, L298N2.12V, VCC2.+
  GND: L298N1.GND, Part2.GND, L298N2.GND, D1.C, D2.C, D3.C, D4.C, D5.C, D6.C, 123sda.GND, Water_Level_Sensor1.GND, VCC1.-
  VIN: L298N1.5V#7, Part2.VIN, 123sda.VDD, R2.Pin_0, Water_Level_Sensor1.VCC
  N5: L298N1.5V#9, L298N1.ENA
  N6: L298N1.5V#10, L298N1.ENB
  N7: L298N1.IN1, Part2.D6_PWM
  N8: L298N1.IN2, Part2.D7_PWM
  N9: L298N1.IN3, Part2.D8_PWM
  N10: L298N1.IN4, Part2.D9_PWM
  N11: Part2.A0, Water_Level_Sensor1.SIG
  N12: Part2.A5, 123sda.CKIN
  N13: Part2.D11_PWM, L298N2.IN2
  N14: Part2.D10_PWM, L298N2.IN1
  N15: Part2.D2_PWM, LED2.anode
  N16: Part2.D3_PWM, LED1.anode
  N17: Part2.D4_PWM, 123sda.DCOUT
  N18: Part2.D5_PWM, 123sda.STROBE
  N19: L298N2.OUT1, M6.pin_1
  N20: L298N2.OUT2, M8.pin_1
  N21: L298N2.5V#9, L298N2.ENA
  N22: L298N2.5V#10, L298N2.ENB
  N23: M3.pin_2, D6.A
  N24: M4.pin_2, D4.A
  N25: M5.pin_2, D5.A
  N26: M6.pin_2, D2.A
  N27: M7.pin_2, D3.A
  N28: M8.pin_2, D1.A

notes:
  VDD
  GND
  Strope
  Reset
  Left
  Right
  Audio GND
  Signal
  AUX

custom parts:
  L298N DC motor driver: 2x DC motor driver with 78M05 positive voltage regulator (7..35 V) L298N: max 46 V, 2 A Set 5 V Enable jumper to enable 5 V regultor (needed for the L298N) and +5 V output at screw terminal or supply external +5 V at screw terminal Set ENA and/or ENB to +5 V to enable motor permanently or supply ENA and/or ENB with PWM signal IN1 and IN2 set rotation directory for motor A (OUT1/OUT2) IN2 and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
  Water Level Sensor: A water level sensor. This sensor operates at 3V to 5V. The Sig (signal) pin outputs an analogue signal that is in proportion to the amount of water in contact with the sensor.
