# Fritzing sketch Circuit-Diagram (saved by Fritzing 0.9.3b)
breadboards: 2

parts:
  Part3 = Arduino Mega 2560 (Rev3)
  L298N3 = L298N DC motor driver
  L298N4 = L298N DC motor driver
  M9 = DC Motor
  M10 = DC Motor
  M11 = DC Motor
  M12 = DC Motor
  M13 = DC Motor
  M14 = DC Motor
  D7 = Diode [package=diode-1n4001]
  D8 = Diode [package=diode-1n4001]
  D9 = Diode [package=diode-1n4001]
  D10 = Diode [package=diode-1n4001]
  D11 = Diode [package=diode-1n4001]
  D12 = Diode [package=diode-1n4001]
  Water_Level_Sensor2 = Water Level Sensor
  LED3 = smd LED [color="Yellow (595nm)" package="0805 [SMD]"]
  LED4 = smd LED [color="Red (633nm)" package="0805 [SMD]"]
  R3 = Resistor [tolerance=±5% resistance=220 package="2010 [SMD]"]
  R4 = Resistor [tolerance=±5% resistance=220 package="2010 [SMD]"]
  123sda1 = MSGEQ7 [package=soic8]
  SPKR1 = Loudspeaker
  TRRS1 = Audio Jack (TRRS) 3.5mm [part_number="LUMBERG JEITA RC-5325A" package="RC-5325A [SMD]"]
  TRRS2 = Audio Jack (TRRS) 3.5mm [part_number="LUMBERG JEITA RC-5325A" package="RC-5325A [SMD]"]  # not connected
  VCC1 = Battery block 9V

nets:
  N1: Part3.A0, Water_Level_Sensor2.SIG
  N2: Part3.A5, 123sda1.CKIN
  N3: Part3.D11_PWM, L298N3.IN2
  N4: Part3.D10_PWM, L298N3.IN1
  N5: Part3.D9_PWM, L298N4.IN4
  N6: Part3.D8_PWM, L298N4.IN3
  GND: Part3.GND, L298N3.GND, L298N4.GND, D7.C, D8.C, D9.C, D10.C, D11.C, D12.C, Water_Level_Sensor2.GND, R3.Pin_0, R4.Pin_0, 123sda1.GND, SPKR1.pin1, VCC1.-
  VIN: Part3.VIN, L298N4.5V#7, Water_Level_Sensor2.VCC, 123sda1.VDD, SPKR1.pin2
  N7: Part3.D2_PWM, LED3.anode
  N8: Part3.D3_PWM, LED4.anode
  N9: Part3.D4_PWM, 123sda1.STROBE
  N10: Part3.D5_PWM, 123sda1.DCOUT
  N11: Part3.D6_PWM, L298N4.IN1
  N12: Part3.D7_PWM, L298N4.IN2
  N13: L298N3.OUT1, M11.pin_1
  N14: L298N3.OUT2, M10.pin_1
  12V: L298N3.12V, L298N4.12V, VCC1.+
  N15: L298N3.5V#9, L298N3.ENA
  N16: L298N3.5V#10, L298N3.ENB
  N17: L298N4.OUT1, M9.pin_1
  N18: L298N4.OUT2, M14.pin_1
  N19: L298N4.OUT3, M13.pin_1
  N20: L298N4.OUT4, M12.pin_1
  N21: L298N4.5V#9, L298N4.ENA
  N22: L298N4.5V#10, L298N4.ENB
  N23: M9.pin_2, D8.A
  N24: M10.pin_2, D7.A
  N25: M11.pin_2, D12.A
  N26: M12.pin_2, D11.A
  N27: M13.pin_2, D10.A
  N28: M14.pin_2, D9.A
  N29: LED3.cathode, R3.Pin_1
  N30: LED4.cathode, R4.Pin_1
  N31: 123sda1.AUDIO_IN, TRRS1.RING2
  N32: 123sda1.CG, TRRS1.RING1
  N33: 123sda1.RESET, TRRS1.SLEEVE

notes:
  Signal
  Audio GND
  Right
  Left
  Reset
  Strobe
  GND
  VDD
  Audio Source
  Male-Male AUX
  The Actual module used was DRF0126
  1Male-2 Female AUX splitter was used

custom parts:
  L298N DC motor driver: 2x DC motor driver with 78M05 positive voltage regulator (7..35 V) L298N: max 46 V, 2 A Set 5 V Enable jumper to enable 5 V regultor (needed for the L298N) and +5 V output at screw terminal or supply external +5 V at screw terminal Set ENA and/or ENB to +5 V to enable motor permanently or supply ENA and/or ENB with PWM signal IN1 and IN2 set rotation directory for motor A (OUT1/OUT2) IN2 and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
  Water Level Sensor: A water level sensor. This sensor operates at 3V to 5V. The Sig (signal) pin outputs an analogue signal that is in proportion to the amount of water in contact with the sensor.
